// Logisim project hack.circ as structural Verilog: 5 circuits, main circuit main
module main (
  input  in_1,
  input  [15:0] in_2,
  input  in_3,
  input  in_4,
  output [15:0] out_5
);

  Counter #(.max('hffff), .width(16)) counter_1 (
    .load(in_1), .D(in_2), .Q(out_5), .clk(in_3), .clr(in_4));  // open: count, carry, up
endmodule

module alu (
  input  [15:0] x,
  input  [15:0] y,
  input  zx,
  input  nx,
  input  zy,
  input  ny,
  input  f,
  input  no,
  output [15:0] o,
  output zr,
  output ng
);

  wire or_1_out;
  wire [15:0] adder_1_out, and_1_out, multiplexer_1_out, multiplexer_2_out, multiplexer_3_out,
       multiplexer_4_out, multiplexer_5_out, not_1_out, not_2_out, not_3_out;

  Multiplexer #(.width(16)) multiplexer_1 (.in0(x), .in1({16{1'b0}}), .out(multiplexer_1_out), .sel(zx));
  Multiplexer #(.width(16)) multiplexer_2 (.in0(y), .in1({16{1'b0}}), .out(multiplexer_2_out), .sel(zy));
  assign not_1_out = ~multiplexer_1_out;  // NOT_Gate not_1, 16 bits wide
  Multiplexer #(.width(16)) multiplexer_3 (.in0(multiplexer_2_out), .in1(not_2_out), .out(multiplexer_3_out), .sel(ny));
  assign not_2_out = ~multiplexer_2_out;  // NOT_Gate not_2, 16 bits wide
  Multiplexer #(.width(16)) multiplexer_4 (.in0(multiplexer_1_out), .in1(not_1_out), .out(multiplexer_4_out), .sel(nx));
  Adder #(.width(16)) adder_1 (.a(multiplexer_4_out), .b(multiplexer_3_out), .out(adder_1_out));  // open: cin, cout
  assign and_1_out = multiplexer_4_out & multiplexer_3_out;  // AND_Gate and_1, 16 bits wide
  Multiplexer #(.width(16)) multiplexer_5 (.in0(and_1_out), .in1(adder_1_out), .out(multiplexer_5_out), .sel(f));
  Multiplexer #(.width(16)) multiplexer_6 (.in0(multiplexer_5_out), .in1(not_3_out), .out({ng, o[14:0]}), .sel(no));
  assign not_3_out = ~multiplexer_5_out;  // NOT_Gate not_3, 16 bits wide
  or or_1 (or_1_out, o[0], o[1], o[2], o[3], o[4], o[5], o[6], o[7], o[8], o[9], o[10], o[11], o[12], o[13], o[14], ng);
  not not_4 (zr, or_1_out);

  assign o[15] = ng;
endmodule

module cpu (
  input  [15:0] instruction,
  input  clk,
  input  [15:0] in_M,
  input  reset,
  output [15:0] out_M,
  output write_M,
  output [14:0] addr_M,
  output [14:0] pc
);

  wire d_condition_1_write_d, not_1_out;
  wire [15:0] D_q, multiplexer_1_out, multiplexer_2_out;
  wire [15:15] A_q;

  Multiplexer #(.width(16)) multiplexer_1 (.in0(out_M), .in1(instruction), .out(multiplexer_1_out), .sel(not_1_out));
  not not_1 (not_1_out, instruction[15]);
  Register #(.width(16)) D (.D(out_M), .en(d_condition_1_write_d), .clk(clk), .Q(D_q));  // open: clr
  D_condition d_condition_1 (.instr(instruction), .write_D(d_condition_1_write_d));
  Register #(.width(16)) A (.D(multiplexer_1_out), .en(not_1_out), .clk(clk), .Q({A_q[15], addr_M}));  // open: clr
  Multiplexer #(.width(16)) multiplexer_2 (.in0({A_q[15], addr_M}), .in1(in_M), .out(multiplexer_2_out));  // open: sel
  Counter #(.max('h7fff), .width(15)) counter_1 (.D(addr_M), .Q(pc), .clk(clk));  // open: load, count, carry, up, clr
  alu alu_1 (.x(D_q), .y(multiplexer_2_out), .o(out_M));  // open: zx, nx, zy, ny, f, no, zr, ng

  // Other names for the same wires on the sheet: instr[15:0] = instruction

  // Notes on the sheet:
  //   это приходит из RAM
endmodule

module D_condition (
  input  [15:0] instr,
  output write_D
);

  and and_1 (write_D, instr[4], instr[15]);
endmodule

module M_condition (
  input  [15:0] instr
);
endmodule
